// Logisim project s-mips.circ as structural Verilog
module RAM (
  input  [15:0] Address,
  input  [31:0] Data_In_0,
  input  [31:0] Data_In_1,
  input  [31:0] Data_In_2,
  input  [31:0] Data_In_3,
  input  [3:0] Mask,
  input  nRead_Write,
  input  Chip_Select,
  input  Reset,
  output [31:0] Data_Out_0,
  output [31:0] Data_Out_1,
  output [31:0] Data_Out_2,
  output [31:0] Data_Out_3,
  output [3:0] Read_Time,
  output [3:0] Write_Time
);

  wire and_2_out, and_3_out, and_4_out, and_5_out, and_6_out, and_7_out, and_8_out, and_9_out, Changed, CLK,
       comparator_2_eq, comparator_3_eq, comparator_4_eq, comparator_5_eq, comparator_6_eq, Count,
       demultiplexer_3_out0, Idle, Idle_q, Load, Load0, Load1, nand_1_out, or_1_out, or_2_out, or_3_out,
       or_4_out, or_5_out, or_6_out, or_7_out, or_8_out, or_9_out, or_10_out, Proc_q, Update_Mem, Zero_Time;
  wire [3:0] counter_1_q, multiplexer_1_out, subtractor_1_out;
  wire [31:0] register_1_q, register_2_q, register_3_q, register_4_q, register_5_q;

  // Probe on 4'b0011
  // Probe on 4'b0010
  Multiplexer #(.width(4), .enable("false")) multiplexer_1 (
    .in0(4'b0011), .in1(4'b0010), .out(multiplexer_1_out), .sel(nRead_Write));
  or or_1 (or_1_out, Idle, Update_Mem);
  or or_2 (or_2_out, ~Chip_Select, Reset);  // OR_Gate
  Subtractor #(.width(4)) subtractor_1 (.a(multiplexer_1_out), .b(4'b0010), .out(subtractor_1_out));  // open: bin, bout
  Demultiplexer #(.enable("false")) demultiplexer_1 (.out0(Idle), .out1(Load0), .in(Idle_q), .sel(Changed));
  D_Flip_Flop u_Idle (.clk(CLK), .D(or_1_out), .Q(Idle_q), .preset(or_2_out));  // open: Qn, en, reset
  // Probe on counter_1_q
  Counter #(.width(4), .max('hf)) counter_1 (
    .load(Load), .D(subtractor_1_out), .count(Count), .Q(counter_1_q), .clk(CLK), .clr(or_3_out));  // open: carry
  or or_3 (or_3_out, ~Chip_Select, Reset);  // OR_Gate
  Comparator #(.width(4), .mode("unsigned")) comparator_1 (
    .a(4'b0000), .b(counter_1_q), .eq(Zero_Time));  // open: gt, lt
  or or_4 (or_4_out, Count, Load0, Load1);
  Register #(.width(32)) register_1 (.D(Data_In_0), .en(Chip_Select), .Q(register_1_q), .clk(CLK), .clr(or_5_out));
  or or_5 (or_5_out, ~Chip_Select, Reset);  // OR_Gate
  Register #(.width(32)) register_2 (.D(Data_In_1), .en(Chip_Select), .Q(register_2_q), .clk(CLK), .clr(or_6_out));
  or or_6 (or_6_out, ~Chip_Select, Reset);  // OR_Gate
  Register #(.width(32)) register_3 (.D(Data_In_2), .en(Chip_Select), .Q(register_3_q), .clk(CLK), .clr(or_7_out));
  or or_7 (or_7_out, ~Chip_Select, Reset);  // OR_Gate
  Register #(.width(32)) register_4 (.D(Data_In_3), .en(Chip_Select), .Q(register_4_q), .clk(CLK), .clr(or_8_out));
  or or_8 (or_8_out, ~Chip_Select, Reset);  // OR_Gate
  Register #(.width(32)) register_5 (
    .D({{11{1'b1}}, nRead_Write, Mask, Address}), .en(Chip_Select), .Q(register_5_q), .clk(CLK),
    .clr(or_9_out));
  or or_9 (or_9_out, ~Chip_Select, Reset);  // OR_Gate
  D_Flip_Flop Proc (.clk(CLK), .D(or_4_out), .Q(Proc_q), .reset(or_10_out));  // open: Qn, preset, en
  or or_10 (or_10_out, ~Chip_Select, Reset);  // OR_Gate
  Demultiplexer #(.enable("false")) demultiplexer_2 (
    .out0(Count), .out1(Update_Mem), .in(demultiplexer_3_out0), .sel(Zero_Time));
  Demultiplexer #(.enable("false")) demultiplexer_3 (
    .out0(demultiplexer_3_out0), .out1(Load1), .in(Proc_q), .sel(Changed));
  Clock clock_1 (.out(CLK));
  Comparator #(.width(32)) comparator_2 (.a(register_1_q), .b(Data_In_0), .eq(comparator_2_eq));  // open: gt, lt
  Comparator #(.width(32)) comparator_3 (.a(register_2_q), .b(Data_In_1), .eq(comparator_3_eq));  // open: gt, lt
  Comparator #(.width(32)) comparator_4 (.a(register_3_q), .b(Data_In_2), .eq(comparator_4_eq));  // open: gt, lt
  Comparator #(.width(32)) comparator_5 (.a(register_4_q), .b(Data_In_3), .eq(comparator_5_eq));  // open: gt, lt
  Comparator #(.width(32)) comparator_6 (
    .a(register_5_q), .b({{11{1'b1}}, nRead_Write, Mask, Address}), .eq(comparator_6_eq));  // open: gt, lt
  nand nand_1 (nand_1_out, comparator_6_eq, comparator_2_eq, comparator_3_eq, comparator_4_eq, comparator_5_eq);
  and and_1 (Changed, nand_1_out, Chip_Select);
  or or_11 (Load, Count, Load1, Load0);
  // Probe on Address
  and and_2 (and_2_out, Mask[0], Update_Mem, nRead_Write);
  and and_3 (and_3_out, Mask[1], Update_Mem, nRead_Write);
  and and_4 (and_4_out, Mask[2], Update_Mem, nRead_Write);
  and and_5 (and_5_out, Mask[3], Update_Mem, nRead_Write);
  // Probe on Data_Out_0
  RAM_part #(.addrWidth(16), .dataWidth(32), .bus("separate")) ram_1 (
    .addr(Address), .din(Data_In_0), .data(Data_Out_0), .str(and_2_out), .sel(Chip_Select), .clk(CLK),
    .ld(and_6_out), .clr(Reset));
  and and_6 (and_6_out, ~nRead_Write, Idle);  // AND_Gate
  RAM_part #(.addrWidth(16), .dataWidth(32), .bus("separate")) ram_2 (
    .addr(Address), .din(Data_In_1), .data(Data_Out_1), .str(and_3_out), .sel(Chip_Select), .clk(CLK),
    .ld(and_7_out), .clr(Reset));
  and and_7 (and_7_out, ~nRead_Write, Idle);  // AND_Gate
  RAM_part #(.addrWidth(16), .dataWidth(32), .bus("separate")) ram_3 (
    .addr(Address), .din(Data_In_2), .data(Data_Out_2), .str(and_4_out), .sel(Chip_Select), .clk(CLK),
    .ld(and_8_out), .clr(Reset));
  and and_8 (and_8_out, ~nRead_Write, Idle);  // AND_Gate
  RAM_part #(.addrWidth(16), .dataWidth(32), .bus("separate")) ram_4 (
    .addr(Address), .din(Data_In_3), .data(Data_Out_3), .str(and_5_out), .sel(Chip_Select), .clk(CLK),
    .ld(and_9_out), .clr(Reset));
  and and_9 (and_9_out, ~nRead_Write, Idle);  // AND_Gate
  // Probe on Data_Out_1
  // Probe on Data_Out_2
  // Probe on Data_Out_3

  assign Read_Time = 4'b0011;
  assign Write_Time = 4'b0010;

  // Other names for the same wires on the sheet: M0 = Mask[0]; M1 = Mask[1]; M2 = Mask[2]; M3 = Mask[3];
  //   RW = nRead_Write; CLR = Reset; CS = Chip_Select; Load2 = Count

  // Notes on the sheet:
  //   NO MODIFICAR
  //   excepto quizás los valores RT y WT
  //   BANK0
  //   BANK1
  //   BANK2
  //   BANK3
endmodule

module S_MIPS (
  input  Kbd_Available,
  input  [6:0] Kbd_ASCII_Data,
  input  [31:0] RAM_Out_0,
  input  [31:0] RAM_Out_1,
  input  Reset,
  input  [31:0] RAM_Out_2,
  input  Clock,
  input  [31:0] RAM_Out_3,
  input  [3:0] Read_Time,
  input  [3:0] Write_Time,
  output Kbd_Enable,
  output [15:0] Address,
  output Kbd_Clear,
  output TTY_Enable,
  output [6:0] TTY_ASCII_Data,
  output Stop,
  output [31:0] RAM_In_0,
  output [31:0] RAM_In_1,
  output [31:0] RAM_In_2,
  output [31:0] RAM_In_3,
  output [3:0] Mask,
  output nRead_Write,
  output Chip_Select
);

  wire ALU_load, Ch_SP, clear_instr, D_load, halt, I_o_D, Instr_load, not_1_out, Pc_En, Pop, Push, R_RAM,
       W_RAM, W_RF;

  not not_1 (not_1_out, Reset);
  Data_Path_MAIN data_path_main_1 (
    .in_4(Clock), .in_5(Instr_load), .in_6(Pc_En), .in_8(D_load), .in_9(Ch_SP), .in_10(Reset),
    .in_11(nRead_Write), .in_15(Kbd_ASCII_Data), .PUSH(Push), .POP(Pop), .Data_W_RAM(RAM_In_0),
    .out_27(Mask), .RAM_Address(Address), .W_RAM(W_RAM), .halt(halt), .R_RAM(R_RAM),
    .tty_data(TTY_ASCII_Data), .in_16(Kbd_Available), .in_17(clear_instr), .in_1(I_o_D), .kbd_en(Kbd_Enable),
    .in_2(RAM_Out_0), .in_3(RAM_Out_2), .in_13(RAM_Out_1), .in_14(RAM_Out_3), .in_7(ALU_load),
    .tty_en(TTY_Enable), .in_12(W_RF));
  Control_Unit_MAIN control_unit_main_1 (
    .in_1(Clock), .in_7(Read_Time), .in_2(R_RAM), .in_3(halt), .in_9(Push), .in_4(Write_Time), .in_8(Reset),
    .in_5(W_RAM), .in_6(Pop), .in_10(not_1_out), .END(Stop), .IR_Load(Instr_load), .DATA_Load(D_load),
    .clr_instr(clear_instr), .I_O_D(I_o_D), .PC_Load(Pc_En), .out_14(nRead_Write), .CS(Chip_Select),
    .Ch_SP(Ch_SP), .W_RF(W_RF), .load_ALU(ALU_load));
  // Probe on RAM_In_0

  assign RAM_In_1 = RAM_In_0;
  assign RAM_In_2 = RAM_In_0;
  assign RAM_In_3 = RAM_In_0;

  // Other names for the same wires on the sheet: CLK = Clock; CLR = Reset; CS = Chip_Select;
  //   KBD_AVAIL = Kbd_Available; KBD_CLR = Kbd_Clear; KBD_DATA[6:0] = Kbd_ASCII_Data; RAM_A[15:0] = Address;
  //   RAM_INPUT_0[31:0] = RAM_In_0; RAM_INPUT_1[31:0] = RAM_In_0; RAM_INPUT_2[31:0] = RAM_In_0;
  //   RAM_INPUT_3[31:0] = RAM_In_0; RAM_MASK[3:0] = Mask; RAM_OUTPUT_0[31:0] = RAM_Out_0;
  //   RAM_OUTPUT_1[31:0] = RAM_Out_1; RAM_OUTPUT_2[31:0] = RAM_Out_2; RAM_OUTPUT_3[31:0] = RAM_Out_3;
  //   RW = nRead_Write; TTY_DATA[6:0] = TTY_ASCII_Data

  // Notes on the sheet:
  //   RAM ADDRESS
  //   DATA FROM RAM
  //   DATA TO RAM
  //   DATA WRITE MASK
  //   RAM TIMING
  //   RAM CONTROL
  //   KEYBOARD
  //   TTY
  //   SEQUENCING
endmodule

module S_MIPS_Board (
  input  DESHABILITAR_DISPATCHER,
  output halt
);

  wire button_1_out, CLK, CS, d_ff_1_q, LCLR, LoadRAM, LoadRAMOn, LW, R_R_W, R_W, ram_dispatcher_1_finished,
       RCS, Reset_out, RST, TTY_EN;
  wire [2:0] KDB;
  wire [3:0] LMask, Mask, ram_1_read_time, ram_1_write_time, RMask;
  wire [6:0] KDB_DATA, TTY_DATA;
  wire [15:0] Addr, LAddr, RAddr;
  wire [31:0] I0, I1, I2, I3, LData, ram_1_data_out_0, ram_1_data_out_1, ram_1_data_out_2, ram_1_data_out_3,
       RI0, RI1, RI2, RI3;

  TTY #(.rows(25), .cols(80)) tty_1 (.data(TTY_DATA), .clk(CLK), .we(TTY_EN), .clr(RST));
  not not_1 (LoadRAMOn, ram_dispatcher_1_finished);
  RAM_Dispatcher ram_dispatcher_1 (
    .WriteTime(ram_1_write_time), .Clock(CLK), .Data(LData), .Address(LAddr), .Mask(LMask),
    .Finished(ram_dispatcher_1_finished), .Write(LW), .CLR(LCLR));
  Keyboard #(.buflen(64)) keyboard_1 (.clk(CLK), .re(KDB[0]), .avail(KDB[2]), .data(KDB_DATA));  // open: clr
  RAM ram_1 (
    .Address(RAddr), .Data_Out_0(ram_1_data_out_0), .Data_Out_1(ram_1_data_out_1),
    .Data_Out_2(ram_1_data_out_2), .Data_Out_3(ram_1_data_out_3), .Data_In_0(RI0), .Data_In_1(RI1),
    .Data_In_2(RI2), .Data_In_3(RI3), .Mask(RMask), .nRead_Write(R_R_W), .Chip_Select(RCS),
    .Read_Time(ram_1_read_time), .Reset(button_1_out), .Write_Time(ram_1_write_time));
  Button button_1 (.out(button_1_out));
  D_Flip_Flop d_ff_1 (.clk(CLK), .D(1'b1), .Q(d_ff_1_q), .reset(Reset_out));  // open: Qn, preset, en
  Button Reset (.out(Reset_out));
  S_MIPS s_mips_1 (
    .Kbd_Enable(KDB[0]), .Address(Addr), .Kbd_Clear(KDB[1]), .Kbd_Available(KDB[2]), .RAM_In_0(I0),
    .Kbd_ASCII_Data(KDB_DATA), .RAM_In_1(I1), .TTY_Enable(TTY_EN), .RAM_In_2(I2), .RAM_In_3(I3),
    .TTY_ASCII_Data(TTY_DATA), .Reset(RST), .RAM_Out_0(ram_1_data_out_0), .Clock(CLK),
    .RAM_Out_1(ram_1_data_out_1), .Stop(halt), .RAM_Out_2(ram_1_data_out_2), .RAM_Out_3(ram_1_data_out_3),
    .Mask(Mask), .Read_Time(ram_1_read_time), .Write_Time(ram_1_write_time), .nRead_Write(R_W),
    .Chip_Select(CS));
  D_Flip_Flop d_ff_2 (.clk(CLK), .D(d_ff_1_q), .Qn(LCLR), .reset(Reset_out));  // open: Q, preset, en
  or or_1 (RST, LCLR, LoadRAM);
  // Probe on ram_1_data_out_0
  Clock clock_1 (.out(CLK));
  // Probe on TTY_DATA
  Multiplexer #(.width(32), .enable("false")) multiplexer_1 (.in0(I0), .in1(LData), .out(RI0), .sel(LoadRAM));
  Multiplexer #(.width(32), .enable("false")) multiplexer_2 (.in0(I1), .in1(LData), .out(RI1), .sel(LoadRAM));
  Multiplexer #(.width(32), .enable("false")) multiplexer_3 (.in0(I2), .in1(LData), .out(RI2), .sel(LoadRAM));
  Multiplexer #(.width(32), .enable("false")) multiplexer_4 (.in0(I3), .in1(LData), .out(RI3), .sel(LoadRAM));
  and and_1 (LoadRAM, ~1'b1, LoadRAMOn);  // AND_Gate
  Multiplexer #(.width(16), .enable("false")) multiplexer_5 (.in0(Addr), .in1(LAddr), .out(RAddr), .sel(LoadRAM));
  Multiplexer #(.width(4), .enable("false")) multiplexer_6 (.in0(Mask), .in1(LMask), .out(RMask), .sel(LoadRAM));
  Multiplexer #(.enable("false")) multiplexer_7 (.in0(CS), .in1(LW), .out(RCS), .sel(LoadRAM));
  Multiplexer #(.enable("false")) multiplexer_8 (.in0(R_W), .in1(LW), .out(R_R_W), .sel(LoadRAM));

  // Notes on the sheet:
  //   NO MODIFICAR
  //   Keyboard
endmodule

module RAM_Dispatcher (
  input  [3:0] WriteTime,
  input  Clock,
  input  CLR,
  output [31:0] Data,
  output [15:0] Address,
  output [3:0] Mask,
  output Finished,
  output Write
);

  wire demultiplexer_2_out1, demultiplexer_3_out1, End, IDLE_q, IncAddr, Load, or_1_out, or_2_out, While_q,
       WriteEnd;
  wire [3:0] counter_1_q;
  wire [31:0] CurrentAddress_q;

  Counter #(.width(32), .max('hffffffff)) CurrentAddress (
    .count(IncAddr), .Q({CurrentAddress_q[31:18], Address, CurrentAddress_q[1:0]}), .clk(Clock), .clr(CLR));  // open: load, D, carry
  or or_1 (or_1_out, IncAddr, demultiplexer_3_out1, Finished);
  D_Flip_Flop IDLE (.clk(Clock), .D(or_1_out), .Q(IDLE_q), .preset(CLR));  // open: Qn, en, reset
  Demultiplexer #(.enable("false")) demultiplexer_1 (.out0(Load), .out1(Finished), .in(IDLE_q), .sel(End));
  D_Flip_Flop While (.clk(Clock), .D(or_2_out), .Q(While_q), .reset(CLR));  // open: Qn, preset, en
  or or_2 (or_2_out, Write, Load);
  RAM_part #(.addrWidth(18), .dataWidth(32)) ram_1 (
    .addr({Address, CurrentAddress_q[1:0]}), .data(Data), .clk(Clock));  // open: sel, ld, clr
  Demultiplexer #(.enable("false")) demultiplexer_2 (
    .out0(Write), .out1(demultiplexer_2_out1), .in(While_q), .sel(WriteEnd));
  Decoder #(.select(2)) decoder_1 (
    .out0(Mask[0]), .out1(Mask[1]), .out2(Mask[2]), .out3(Mask[3]), .sel(CurrentAddress_q[1:0]));  // open: en
  Demultiplexer #(.enable("false")) demultiplexer_3 (
    .out0(IncAddr), .out1(demultiplexer_3_out1), .in(demultiplexer_2_out1), .sel(End));
  Counter #(.width(4), .max('hf)) counter_1 (
    .load(Load), .D(WriteTime), .count(Write), .Q(counter_1_q), .clk(Clock));  // open: carry, clr
  Comparator #(.width(32)) comparator_1 (.a(Data), .b({32{1'b1}}), .eq(End));  // open: gt, lt
  Comparator #(.width(4)) comparator_2 (.a(4'b0000), .b(counter_1_q), .eq(WriteEnd));  // open: gt, lt

  // Other names for the same wires on the sheet: CLK = Clock; Count = Write; WT[3:0] = WriteTime
endmodule

module Data_Path_MAIN (
  input  in_1,
  input  [31:0] in_2,
  input  [31:0] in_3,
  input  in_4,
  input  in_5,
  input  in_6,
  input  in_7,
  input  in_8,
  input  in_9,
  input  in_10,
  input  in_11,
  input  in_12,
  input  [31:0] in_13,
  input  [31:0] in_14,
  input  [6:0] in_15,
  input  in_16,
  input  in_17,
  output W_RAM,
  output PUSH,
  output halt,
  output POP,
  output kbd_en,
  output R_RAM,
  output [31:0] Data_W_RAM,
  output [6:0] tty_data,
  output [15:0] RAM_Address,
  output [3:0] out_27,
  output tty_en
);

  wire and_1_out, flag_condition_1_flag_condition, Hi_Lo_Load, Hi_Low_Selector, I,
       instruction_decoder_main_1_rdm, instruction_decoder_main_1_sw, J, jr, jumper_main_1_out_7, lw, N_flag,
       R, R_W_RF, tty_en_t, tunnel;
  wire [1:0] A_Selector, B_Selector, multiplexer_2_out, priority_encoder_1_out, RF_DI_Selector;
  wire [3:0] Op_Selector;
  wire [4:0] multiplexer_1_out, multiplexer_3_out, Rd, Rs, Rt;
  wire [5:0] instruction_decoder_main_1_func_code, Op_code;
  wire [6:0] multiplexer_8_out;
  wire [15:0] instruction_decoder_main_1_const, RAM_R_Address, RAM_W_Address;
  wire [25:0] dest;
  wire [31:0] alu_1_carry, ALU_OUT, ALU_R, B, branch_control_main_1_pc_prime, demultiplexer_1_out0,
       demultiplexer_1_out1, hi_and_low_1_hi, hi_and_low_1_low, Hi_Low,
       instruction_fetcher_main_1_instruction, jumper_main_1_jmp_size, k, Keyboard_OUT, Keyboard_Out_t,
       multiplexer_4_out, multiplexer_7_out, multiplexer_9_out, multiplexer_10_out, PC, RAM_OUT,
       random_1_out, register_1_q, SP;
  wire [31:7] A;

  Jumper_MAIN jumper_main_1 (
    .k(k), .Rs({A, tty_data}), .jr(jr), .J(J), .jmp_size(jumper_main_1_jmp_size), .PC(PC), .dest(dest),
    .out_7(jumper_main_1_out_7));
  Flag_Condition_2 flag_condition_1 (
    .OP_Code(Op_code), .Equal_Flag(tunnel), .Less_than_0(N_flag),
    .Flag_Condition(flag_condition_1_flag_condition));
  Multiplexer #(.width(5), .enable("false")) multiplexer_1 (.in0(Rd), .in1(Rt), .out(multiplexer_1_out), .sel(I));
  Random #(.width(32)) random_1 (.clk(in_4), .out(random_1_out));  // open: next, clr
  Multiplexer #(.width(2), .enable("false")) multiplexer_2 (
    .in0(RF_DI_Selector), .in1(2'b00), .out(multiplexer_2_out), .sel(in_9));
  Branch_Control_MAIN branch_control_main_1 (
    .PC(PC), .JZ(jumper_main_1_jmp_size), .PC_prime(branch_control_main_1_pc_prime),
    .jmp(jumper_main_1_out_7), .FC(flag_condition_1_flag_condition));
  Multiplexer #(.width(5), .enable("false")) multiplexer_3 (
    .in0(multiplexer_1_out), .in1({5{1'b1}}), .out(multiplexer_3_out), .sel(in_9));
  Multiplexer #(.select(2), .width(32), .enable("false")) multiplexer_4 (
    .in0(ALU_OUT), .in1(Keyboard_OUT), .in2(random_1_out), .in3(RAM_OUT), .out(multiplexer_4_out),
    .sel(multiplexer_2_out));
  // Probe on multiplexer_2_out
  // Probe on PC
  Multiplexer #(.width(32), .disabled(0), .enable("false")) multiplexer_5 (
    .in0(B), .in1({A, tty_data}),
    .out({Data_W_RAM[7:0], Data_W_RAM[15:8], Data_W_RAM[23:16], Data_W_RAM[31:24]}), .sel(PUSH));
  Program_Counter_MAIN program_counter_main_1 (
    .PC_prime(branch_control_main_1_pc_prime), .in_2(in_6), .in_3(in_10), .in_4(in_4), .PC(PC));
  RAM_Writer_MAIN ram_writer_main_1 (.in_1(ALU_R), .mask(out_27), .adr(RAM_W_Address));
  Multiplexer #(.width(16), .enable("false")) multiplexer_6 (
    .in0(RAM_R_Address), .in1(RAM_W_Address), .out(RAM_Address), .sel(in_11));
  Register_File_MAIN register_file_main_1 (
    .in_1(in_4), .in_2(multiplexer_3_out), .in_3(multiplexer_4_out), .in_4(in_10), .in_5(Rs),
    .in_6(and_1_out), .in_7(Rt), .A({A, tty_data}), .B(B), .SP(SP));
  and and_1 (and_1_out, in_12, R_W_RF);
  Multiplexer #(.select(2), .width(32), .enable("false")) multiplexer_7 (
    .in0(PC), .in1(ALU_R), .in2(SP), .out(multiplexer_7_out), .sel(priority_encoder_1_out));  // open: in3
  Priority_Encoder #(.select(2)) priority_encoder_1 (
    .in0(1'b1), .in1(lw), .in2(POP), .out(priority_encoder_1_out));  // open: in3
  Instruction_Fetcher_MAIN instruction_fetcher_main_1 (
    .in_1(multiplexer_7_out), .in_2(in_2), .in_3(in_13), .in_4(in_3), .in_5(in_14),
    .RAM_Address(RAM_R_Address), .Instruction(instruction_fetcher_main_1_instruction));
  // Probe on B
  Multiplexer #(.width(7), .disabled(0), .enable("false")) multiplexer_8 (
    .in0({7{1'b1}}), .in1(in_15), .out(multiplexer_8_out), .sel(in_16));
  // Probe on multiplexer_9_out
  Multiplexer #(.select(2), .width(32), .enable("false")) multiplexer_9 (
    .in0({A, tty_data}), .in1(SP), .in2(Hi_Low), .out(multiplexer_9_out), .sel(A_Selector));  // open: in3
  Multiplexer #(.select(2), .width(32), .enable("false")) multiplexer_10 (
    .in0(B), .in1(32'h4), .in2(k), .in3({32{1'b0}}), .out(multiplexer_10_out), .sel(B_Selector));
  // Probe on multiplexer_10_out
  assign Keyboard_Out_t = {{25{1'b0}}, multiplexer_8_out};  // Bit_Extender bit_extender_1
  Demultiplexer #(.width(32), .enable("false")) demultiplexer_1 (
    .out0(demultiplexer_1_out0), .out1(demultiplexer_1_out1), .in(instruction_fetcher_main_1_instruction),
    .sel(in_1));
  ALU_2 alu_1 (
    .in_1(multiplexer_9_out), .in_2(multiplexer_10_out), .S(Op_Selector), .Output(ALU_R), .Equal(tunnel),
    .Carry(alu_1_carry), .Less_than_0(N_flag));  // open: Zero_Flag, Carry_Flag, Overflow
  // Probe on register_1_q
  // Probe on Op_Selector
  and and_2 (tty_en, tty_en_t, in_7);
  Register #(.width(32), .trigger("falling")) register_1 (
    .D(demultiplexer_1_out0), .en(in_5), .Q(register_1_q), .clk(in_4), .clr(in_17));
  Register #(.width(32)) register_2 (.D(demultiplexer_1_out1), .en(in_8), .Q(RAM_OUT), .clk(in_4));  // open: clr
  // Probe on ALU_R
  or or_1 (W_RAM, PUSH, instruction_decoder_main_1_sw);
  Instruction_Decoder_MAIN instruction_decoder_main_1 (
    .Instruction(register_1_q), .Op_Code(Op_code), .Rs(Rs), .Rt(Rt), .Rd(Rd),
    .Const(instruction_decoder_main_1_const), .Dest_salto(dest),
    .Func_Code(instruction_decoder_main_1_func_code), .R(R), .I(I), .J(J), .halt(halt), .tty(tty_en_t),
    .kbd_en(kbd_en), .push(PUSH), .pop(POP), .sw(instruction_decoder_main_1_sw), .lw(lw), .jr(jr),
    .rdm(instruction_decoder_main_1_rdm), .RF_W(R_W_RF), .Load_HiLo(Hi_Lo_Load), .HiLo_Sel(Hi_Low_Selector));
  // Priority_Encoder #(.select(2)) priority_encoder_2: pin names not known; wires that end beside it: Op_Selector, 1'b1, kbd_en, RF_DI_Selector, instruction_decoder_main_1_rdm, R_RAM
  Register #(.width(32), .trigger("falling")) register_3 (.D(ALU_R), .en(in_7), .Q(ALU_OUT), .clk(in_4));  // open: clr
  or or_2 (R_RAM, lw, POP);
  Hi_and_Low hi_and_low_1 (
    .in_1(in_4), .in_2(in_10), .D_Low(ALU_OUT), .D_Hi(alu_1_carry), .Low(hi_and_low_1_low),
    .Hi(hi_and_low_1_hi), .in_3(Hi_Lo_Load));
  Multiplexer #(.width(32), .enable("false")) multiplexer_11 (
    .in0(hi_and_low_1_low), .in1(hi_and_low_1_hi), .out(Hi_Low), .sel(Hi_Low_Selector));
  ALU_Decoder_2 alu_decoder_1 (
    .OP_Code(Op_code), .Func_Code(instruction_decoder_main_1_func_code), .AS(A_Selector), .BS(B_Selector),
    .OP_Selector(Op_Selector));
  // Probe on Op_Selector
  Constant_Completer_MAIN constant_completer_main_1 (.in_1(Op_code), .in_2(instruction_decoder_main_1_const), .k(k));

  // Other names for the same wires on the sheet: A[6:0] = tty_data; Ch_SP = in_9; clear_instr = in_17; clk = in_4;
  //   Data_L = in_8; Data_RAM_1[31:0] = in_2; Data_RAM_2[31:0] = in_13; Data_RAM_3[31:0] = in_3;
  //   Data_RAM_4[31:0] = in_14; I_o_D = in_1; Instr_L = in_5; kbd_av = in_16; keyboard_data[6:0] = in_15;
  //   load_ALU = in_7; mask[3:0] = out_27; PC_en = in_6; RAM_R_W = in_11; rst = in_10; W_RF_sig = in_12

  // Notes on the sheet:
  //   Inputs
  //   Outputs
  //   Data Path
endmodule

module ALU_Decoder_2 (
  input  [5:0] OP_Code,
  input  [5:0] Func_Code,
  output [1:0] AS,
  output [1:0] BS,
  output [3:0] OP_Selector
);

  wire _0000, _00_0001, _00_0110, _00_0111, _00_1000, _00_1010, _00_1011, _00_1100, _00_1101, _00_1110,
       _0001, _01_0000, _01_0010, _0010, _0011, _0100, _0101, _0110, _0111, _1000, _1001, _1010, _1011,
       and_2_out, and_4_out, and_12_out, and_13_out, and_14_out, and_15_out, and_16_out, and_17_out,
       and_18_out, and_19_out, and_20_out, and_21_out, and_24_out, and_26_out, and_28_out, and_29_out,
       and_31_out, and_32_out, and_34_out, and_35_out, and_36_out, and_37_out, and_38_out, and_39_out,
       and_40_out, and_42_out, and_43_out, comparator_1_eq, comparator_2_eq, comparator_3_eq,
       comparator_4_eq, comparator_5_eq, MF, no_op, OP_00_0000, OP_11_1000, or_1_out, or_4_out, or_5_out,
       xor_1_out, xor_2_out;

  and and_1 (OP_11_1000, ~OP_Code[0], ~OP_Code[1], ~OP_Code[2], OP_Code[3], OP_Code[4], OP_Code[5]);  // AND_Gate
  and and_2 (and_2_out, ~Func_Code[0], ~Func_Code[1], ~Func_Code[2], ~Func_Code[3], ~Func_Code[4], ~Func_Code[5]);  // AND_Gate
  and and_3 (OP_00_0000, ~OP_Code[0], ~OP_Code[1], ~OP_Code[2], ~OP_Code[3], ~OP_Code[4], ~OP_Code[5]);  // AND_Gate
  and and_4 (and_4_out, ~Func_Code[0], ~Func_Code[1], ~Func_Code[2], ~Func_Code[3], ~Func_Code[4], Func_Code[5]);  // AND_Gate
  and and_5 (_00_1000, ~OP_Code[0], ~OP_Code[1], ~OP_Code[2], OP_Code[3], ~OP_Code[4], ~OP_Code[5]);  // AND_Gate
  and and_6 (_01_0000, ~Func_Code[0], ~Func_Code[1], ~Func_Code[2], ~Func_Code[3], Func_Code[4], ~Func_Code[5]);  // AND_Gate
  and and_7 (_01_0010, ~Func_Code[0], Func_Code[1], ~Func_Code[2], ~Func_Code[3], Func_Code[4], ~Func_Code[5]);  // AND_Gate
  and and_8 (_00_0111, OP_Code[0], OP_Code[1], OP_Code[2], ~OP_Code[3], ~OP_Code[4], ~OP_Code[5]);  // AND_Gate
  and and_9 (_00_1010, ~OP_Code[0], OP_Code[1], ~OP_Code[2], OP_Code[3], ~OP_Code[4], ~OP_Code[5]);  // AND_Gate
  and and_10 (_00_0110, ~OP_Code[0], OP_Code[1], OP_Code[2], ~OP_Code[3], ~OP_Code[4], ~OP_Code[5]);  // AND_Gate
  and and_11 (_00_0001, OP_Code[0], ~OP_Code[1], ~OP_Code[2], ~OP_Code[3], ~OP_Code[4], ~OP_Code[5]);  // AND_Gate
  Comparator #(.width(6)) comparator_1 (.a(OP_Code), .b(6'b100011), .eq(comparator_1_eq));  // open: gt, lt
  Comparator #(.width(6)) comparator_2 (.a(OP_Code), .b(6'b101011), .eq(comparator_2_eq));  // open: gt, lt
  and and_12 (and_12_out, ~Func_Code[0], Func_Code[1], ~Func_Code[2], ~Func_Code[3], ~Func_Code[4], Func_Code[5]);  // AND_Gate
  and and_13 (and_13_out, Func_Code[0], ~Func_Code[1], ~Func_Code[2], ~Func_Code[3], ~Func_Code[4], ~Func_Code[5]);  // AND_Gate
  and and_14 (and_14_out, ~Func_Code[0], ~Func_Code[1], ~Func_Code[2], Func_Code[3], Func_Code[4], ~Func_Code[5]);  // AND_Gate
  and and_15 (and_15_out, Func_Code[0], ~Func_Code[1], ~Func_Code[2], Func_Code[3], Func_Code[4], ~Func_Code[5]);  // AND_Gate
  and and_16 (and_16_out, OP_00_0000, and_12_out);
  and and_17 (and_17_out, OP_11_1000, and_13_out);
  and and_18 (and_18_out, OP_11_1000, and_2_out);
  and and_19 (and_19_out, OP_00_0000, and_4_out);
  and and_20 (and_20_out, OP_00_0000, _01_0000);
  and and_21 (and_21_out, OP_00_0000, _01_0010);
  or or_1 (or_1_out, _00_0001, comparator_1_eq, comparator_2_eq);
  or or_2 (_0101, and_16_out, and_17_out);
  and and_22 (_0110, OP_00_0000, and_14_out);
  and and_23 (_1000, OP_00_0000, and_15_out);
  or or_3 (_0100, and_18_out, _00_1000, and_19_out, and_20_out, and_21_out, _00_0111, _00_1010, _00_0110, or_1_out);
  or or_4 (or_4_out, _00_1000, _00_1100, _00_1101, _00_1110, _00_1010, _00_1011);
  Priority_Encoder #(.select(4), .disabled(0)) priority_encoder_1 (
    .in0(_0000), .in1(_0001), .in2(_0010), .in3(_0011), .in4(_0100), .in5(_0101), .in6(_0110), .in7(_0111),
    .in8(_1000), .in9(_1001), .in10(_1010), .in11(_1011), .in13(no_op), .out(OP_Selector));  // open: in12, in14, in15, gs, en_out, en_in
  Comparator #(.width(6)) comparator_3 (.a(OP_Code), .b({6{1'b0}}), .eq(comparator_3_eq));  // open: gt, lt
  and and_24 (and_24_out, ~Func_Code[0], ~Func_Code[1], Func_Code[2], ~Func_Code[3], ~Func_Code[4], Func_Code[5]);  // AND_Gate
  and and_25 (_00_1100, ~OP_Code[0], ~OP_Code[1], OP_Code[2], OP_Code[3], ~OP_Code[4], ~OP_Code[5]);  // AND_Gate
  and and_26 (and_26_out, Func_Code[0], ~Func_Code[1], Func_Code[2], ~Func_Code[3], ~Func_Code[4], Func_Code[5]);  // AND_Gate
  and and_27 (_00_1101, OP_Code[0], ~OP_Code[1], OP_Code[2], OP_Code[3], ~OP_Code[4], ~OP_Code[5]);  // AND_Gate
  and and_28 (and_28_out, Func_Code[0], Func_Code[1], Func_Code[2], ~Func_Code[3], ~Func_Code[4], Func_Code[5]);  // AND_Gate
  and and_29 (and_29_out, ~Func_Code[0], ~Func_Code[1], ~Func_Code[2], Func_Code[3], ~Func_Code[4], Func_Code[5]);  // AND_Gate
  and and_30 (_00_1110, ~OP_Code[0], OP_Code[1], OP_Code[2], OP_Code[3], ~OP_Code[4], ~OP_Code[5]);  // AND_Gate
  and and_31 (and_31_out, ~Func_Code[0], Func_Code[1], ~Func_Code[2], Func_Code[3], ~Func_Code[4], Func_Code[5]);  // AND_Gate
  and and_32 (and_32_out, Func_Code[0], Func_Code[1], ~Func_Code[2], Func_Code[3], ~Func_Code[4], Func_Code[5]);  // AND_Gate
  and and_33 (_00_1011, OP_Code[0], OP_Code[1], ~OP_Code[2], OP_Code[3], ~OP_Code[4], ~OP_Code[5]);  // AND_Gate
  and and_34 (and_34_out, ~OP_Code[0], ~OP_Code[1], OP_Code[2], ~OP_Code[3], ~OP_Code[4], ~OP_Code[5]);  // AND_Gate
  and and_35 (and_35_out, OP_Code[0], ~OP_Code[1], OP_Code[2], ~OP_Code[3], ~OP_Code[4], ~OP_Code[5]);  // AND_Gate
  and and_36 (and_36_out, ~Func_Code[0], Func_Code[1], ~Func_Code[2], Func_Code[3], Func_Code[4], ~Func_Code[5]);  // AND_Gate
  and and_37 (and_37_out, Func_Code[0], Func_Code[1], ~Func_Code[2], Func_Code[3], Func_Code[4], ~Func_Code[5]);  // AND_Gate
  Comparator #(.width(6)) comparator_4 (.a(Func_Code), .b({6{1'b0}}), .eq(comparator_4_eq));  // open: gt, lt
  Comparator #(.width(6)) comparator_5 (.a(OP_Code), .b({6{1'b1}}), .eq(comparator_5_eq));  // open: gt, lt
  ExactlyOne xor_1 (.out(xor_1_out), .in0(1'b1), .in1(OP_11_1000), .in2(MF));
  Priority_Encoder #(.select(2)) priority_encoder_2 (
    .in0(xor_1_out), .in1(OP_11_1000), .in2(MF), .out(AS));  // open: in3, gs, en_out, en_in
  ExactlyOne xor_2 (.out(xor_2_out), .in0(1'b1), .in1(OP_11_1000), .in2(or_4_out), .in3(or_5_out));
  Priority_Encoder #(.select(2)) priority_encoder_3 (
    .in0(xor_2_out), .in1(OP_11_1000), .in2(or_4_out), .in3(or_5_out), .out(BS));  // open: gs, en_out, en_in
  or or_5 (or_5_out, _00_0110, _00_0111, _00_0001, _01_0000, _01_0010);
  or or_6 (MF, _01_0000, _01_0010);
  and and_38 (and_38_out, OP_00_0000, and_24_out);
  and and_39 (and_39_out, OP_00_0000, and_26_out);
  and and_40 (and_40_out, OP_00_0000, and_29_out);
  and and_41 (_1010, OP_00_0000, and_31_out);
  and and_42 (and_42_out, OP_00_0000, and_32_out);
  and and_43 (and_43_out, comparator_3_eq, comparator_4_eq);
  or or_7 (no_op, and_43_out, comparator_5_eq);
  or or_8 (_0000, and_38_out, _00_1100);
  or or_9 (_0001, and_39_out, _00_1101);
  and and_44 (_0011, OP_00_0000, and_28_out);
  or or_10 (_0010, and_40_out, _00_1110);
  or or_11 (_1011, and_42_out, _00_1011, and_34_out, and_35_out);
  and and_45 (_0111, OP_00_0000, and_36_out);
  and and_46 (_1001, OP_00_0000, and_37_out);

  // Other names for the same wires on the sheet: OP_S[3:0] = OP_Selector

  // Notes on the sheet:
  //   Op Code
  //   00 0000
  //   00 0000
  //   00 0000
  //   00 0000
  //   00 0000
  //   00 0000
  //   00 0000
  //   00 1110
  //   00 0000
  //   00 1010
  //   00 0101
  //   11 1000
  //   00 0000
  //   00 1000
  //   00 0000
  //   00 0000
  //   00 1100
  //   00 1101
  //   00 0000
  //   00 1011
  //   00 0100
  //   00 0110
  //   00 0111
  //   00 0001
  //   11 1000
  //   00 0000
  //   00 0000
  //   Func Code
  //   10 0000
  //   10 0010
  //   01 1000
  //   01 1001
  //   01 1010
  //   01 1011
  //   x
  //   10 0100
  //   10 0101
  //   10 0111
  //   10 1000
  //   x
  //   x
  //   x
  //   10 1010
  //   10 1011
  //   x
  //   x
  //   x
  //   x
  //   x
  //   x
  //   x
  //   00 0000
  //   00 0001
  //   01 0000
  //   01 0010
  //   AS
  //   00
  //   00
  //   00
  //   00
  //   00
  //   00
  //   00
  //   00
  //   00
  //   00
  //   00
  //   00
  //   00
  //   00
  //   00
  //   00
  //   00
  //   00
  //   00
  //   00
  //   00
  //   00
  //   00
  //   01
  //   01
  //   10
  //   10
  //   BS
  //   00
  //   00
  //   00
  //   00
  //   00
  //   00
  //   10
  //   00
  //   00
  //   00
  //   00
  //   10
  //   10
  //   10
  //   00
  //   00
  //   10
  //   10
  //   00
  //   00
  //   11
  //   11
  //   11
  //   01
  //   01
  //   11
  //   11
  //   0100
  //   0101
  //   0110
  //   1000
  //   0111
  //   1001
  //   0100
  //   0000
  //   0001
  //   0110
  //   Op Selector
  //   0011
  //   0010
  //   0000
  //   0001
  //   0010
  //   1010
  //   1011
  //   1010
  //   1011
  //   1011
  //   0100
  //   1010
  //   1010
  //   1010
  //   0100
  //   0101
  //   0100
  //   0100
  //   0101
  //   1000
  //   Name
  //   add
  //   sub
  //   mult
  //   mulu
  //   div
  //   divu
  //   addi
  //   and
  //   or
  //   nor
  //   xor
  //   andi
  //   ori
  //   xori
  //   slt
  //   sltu
  //   slti
  //   sltiu
  //   beq
  //   bne
  //   blez
  //   bgtz
  //   bltz
  //   pop
  //   push
  //   mfhi
  //   mflo
  //   0100
  //   Entradas
  //   Salidas
  //   0000
  //   0001
  //   0011
  //   0010
  //   1010
  //   1011
  //   0111
  //   1001
endmodule

module ALU_2 (
  input  [31:0] in_1,
  input  [31:0] in_2,
  input  [3:0] S,
  output [31:0] Output,
  output Zero_Flag,
  output Carry_Flag,
  output Overflow,
  output Equal,
  output Less_than_0,
  output [31:0] Carry
);

  wire comparator_1_lt, comparator_2_lt;
  wire [1:0] CF_OF, CF_OF_t;
  wire [31:0] ADD, AND, C_Out_uX, C_Out_X, DIV, MULT, NOR, OR, Resto, Resto_u, STL, STLU, SUB, UDIV, UMULT,
       XOR;

  assign AND = in_1 & in_2;  // AND_Gate and_1, 32 bits wide
  assign OR = in_1 | in_2;  // OR_Gate or_1, 32 bits wide
  assign XOR = in_1 ^ in_2;  // XOR_Gate xor_1, 32 bits wide
  assign NOR = ~(in_1 | in_2);  // NOR_Gate nor_1, 32 bits wide
  Comparator #(.width(32)) comparator_1 (.a(in_1), .b(in_2), .lt(comparator_1_lt));  // open: gt, eq
  Comparator #(.width(32), .mode("unsigned")) comparator_2 (
    .a(in_1), .b(in_2), .eq(Equal), .lt(comparator_2_lt));  // open: gt
  assign STL = {{31{1'b0}}, comparator_1_lt};  // Bit_Extender bit_extender_1
  assign STLU = {{31{1'b0}}, comparator_2_lt};  // Bit_Extender bit_extender_2
  Overflow_Add overflow_add_1 (
    .in_1(in_1), .out_4(ADD), .in_2(in_2), .out_5(CF_OF[1]), .out_6(CF_OF[0]));  // open: in_3
  Overflow_Sub overflow_sub_1 (
    .in_1(in_1), .out_4(SUB), .in_2(in_2), .out_5(CF_OF_t[1]), .out_6(CF_OF_t[0]));  // open: in_3
  Multiplier #(.width(32)) multiplier_1 (.a(in_1), .b(in_2), .out(MULT), .cout(C_Out_X));  // open: cin
  Divider #(.width(32)) divider_1 (.a(in_1), .b(in_2), .out(DIV), .rem(Resto));  // open: upper
  Unsigned_Mult unsigned_mult_1 (.A(in_1), .Output(UMULT), .B(in_2), .Carry_Out(C_Out_uX));
  // Unsigned_Div unsigned_div_1: pin names not known; wires that end beside it: in_1, in_2, Resto_u, UDIV
  Multiplexer #(.select(4), .width(32)) multiplexer_1 (
    .in0(AND), .in1(OR), .in2(XOR), .in3(NOR), .in4(ADD), .in5(SUB), .in6(MULT), .in7(DIV), .in8(UMULT),
    .in9(UDIV), .in10(STL), .in11(STLU), .in12({32{1'b0}}), .in13({32{1'b0}}), .in14({32{1'b0}}),
    .in15({32{1'b0}}), .out(Output), .sel(S));  // open: en
  Multiplexer #(.select(4), .width(2)) multiplexer_2 (
    .in0(2'b00), .in1(2'b00), .in2(2'b00), .in3(2'b00), .in4(CF_OF), .in5(CF_OF_t), .in6(2'b00), .in7(2'b00),
    .in8(2'b00), .in9(2'b00), .in10(2'b00), .in11(2'b00), .in12(2'b00), .in13(2'b00), .in14(2'b00),
    .in15(2'b00), .out({Carry_Flag, Overflow}), .sel(S));  // open: en
  Multiplexer #(.select(4), .width(32)) multiplexer_3 (
    .in0({32{1'b0}}), .in1({32{1'b0}}), .in2({32{1'b0}}), .in3({32{1'b0}}), .in4({32{1'b0}}),
    .in5({32{1'b0}}), .in6(C_Out_X), .in7(Resto), .in8(C_Out_uX), .in9(Resto_u), .in10({32{1'b0}}),
    .in11({32{1'b0}}), .in12({32{1'b0}}), .in13({32{1'b0}}), .in14({32{1'b0}}), .in15({32{1'b0}}),
    .out(Carry), .sel(S));  // open: en
  // Probe on Output
  Comparator #(.width(32)) comparator_3 (.a(Output), .b({32{1'b0}}), .eq(Zero_Flag), .lt(Less_than_0));  // open: gt

  // Other names for the same wires on the sheet: OF = Overflow; CF = Carry_Flag; A[31:0] = in_1; B[31:0] = in_2;
  //   EQ = Equal; EXT[31:0] = Carry; LT_0 = Less_than_0; OTPT[31:0] = Output; ZF = Zero_Flag

  // Notes on the sheet:
  //   Entrada A
  //   Entrada B
  //   Selector
  //   Instrucciones Logicas
  //   Instrucciones de Comparacion
  //   Instrucciones Aritmeticas
endmodule

module Overflow_Add (
  input  [31:0] in_1,
  input  [31:0] in_2,
  input  in_3,
  output [31:0] out_4,
  output out_5,
  output out_6
);

  wire adder_1_cout;

  Adder #(.width(31)) adder_1 (.a(in_1[30:0]), .b(in_2[30:0]), .out(out_4[30:0]), .cin(in_3), .cout(adder_1_cout));
  Adder #(.width(1)) adder_2 (.a(in_1[31]), .b(in_2[31]), .out(out_4[31]), .cin(adder_1_cout), .cout(out_5));
  xor xor_1 (out_6, adder_1_cout, out_5);

  // Other names for the same wires on the sheet: A[31:0] = in_1; B[31:0] = in_2; c_in = in_3; CF = out_5; OF = out_6;
  //   Result[31:0] = out_4
endmodule

module Overflow_Sub (
  input  [31:0] in_1,
  input  [31:0] in_2,
  input  in_3,
  output [31:0] out_4,
  output out_5,
  output out_6
);

  wire subtractor_1_bout;

  Subtractor #(.width(31)) subtractor_1 (
    .a(in_1[30:0]), .b(in_2[30:0]), .out(out_4[30:0]), .bin(in_3), .bout(subtractor_1_bout));
  Subtractor #(.width(1)) subtractor_2 (
    .a(in_1[31]), .b(in_2[31]), .out(out_4[31]), .bin(subtractor_1_bout), .bout(out_5));
  xor xor_1 (out_6, subtractor_1_bout, out_5);

  // Other names for the same wires on the sheet: A[31:0] = in_1; B[31:0] = in_2; b_in = in_3; CF = out_5; OF = out_6;
  //   Result[31:0] = out_4
endmodule

module Unsigned_Mult (
  input  [31:0] A,
  input  [31:0] B,
  output [31:0] Output,
  output [31:0] Carry_Out
);

  wire [31:0] valor_absoluto_1_output, valor_absoluto_2_output;

  Valor_Absoluto valor_absoluto_1 (.Input(A), .Output(valor_absoluto_1_output));
  Valor_Absoluto valor_absoluto_2 (.Input(B), .Output(valor_absoluto_2_output));
  Multiplier #(.width(32)) multiplier_1 (
    .a(valor_absoluto_1_output), .b(valor_absoluto_2_output), .out(Output), .cout(Carry_Out));  // open: cin
endmodule

module Unsigned_Div (
  input  [31:0] in_1,
  input  [31:0] in_2,
  output [31:0] Lo,
  output [31:0] Hi
);

  wire [31:0] _00, _00_hi, _01, _01_hi, _10, _10_hi, _11, _11_hi, divider_2_out, divider_3_out,
       negator_1_out, negator_3_out, negator_4_out, negator_5_out;

  // Probe on in_1
  // Probe on in_2
  Multiplexer #(.select(2), .width(32), .enable("false")) multiplexer_1 (
    .in0(_00), .in1(_01), .in2(_10), .in3(_11), .out(Lo), .sel({in_1[31], in_2[31]}));
  // Probe on Lo
  Multiplexer #(.select(2), .width(32), .enable("false")) multiplexer_2 (
    .in0(_00_hi), .in1(_01_hi), .in2(_10_hi), .in3(_11_hi), .out(Hi), .sel({in_1[31], in_2[31]}));
  // Probe on Hi
  // Probe on in_1
  // Probe on in_2
  // Probe on in_1
  // Probe on in_2
  // Probe on in_1
  // Probe on in_2
  Divider #(.width(32)) divider_1 (.a(in_1), .b(in_2), .out(_00), .rem(_00_hi));  // open: upper
  Negator #(.width(32)) negator_1 (.in(in_1), .out(negator_1_out));
  // Probe on _00
  Divider #(.width(32)) divider_2 (.a(negator_1_out), .b(in_2), .out(divider_2_out), .rem(_10_hi));  // open: upper
  // Probe on divider_2_out
  // Probe on _10_hi
  Negator #(.width(32)) negator_2 (.in(divider_2_out), .out(_10));
  // Probe on in_1
  // Probe on in_2
  // Probe on _10
  Divider #(.width(32)) divider_3 (.a(in_1), .b(negator_3_out), .out(divider_3_out), .rem(_01_hi));  // open: upper
  Negator #(.width(32)) negator_3 (.in(in_2), .out(negator_3_out));
  // Probe on in_1
  // Probe on in_2
  // Probe on divider_3_out
  Negator #(.width(32)) negator_4 (.in(in_1), .out(negator_4_out));
  Negator #(.width(32)) negator_5 (.in(in_2), .out(negator_5_out));
  Negator #(.width(32)) negator_6 (.in(divider_3_out), .out(_01));
  // Probe on _01
  Divider #(.width(32)) divider_4 (.a(negator_4_out), .b(negator_5_out), .out(_11), .rem(_11_hi));  // open: upper
  // Probe on _11_hi
  // Probe on _11

  // Other names for the same wires on the sheet: A[31:0] = in_1; BMS_A = in_1[31]; B[31:0] = in_2; BMS_B = in_2[31]

  // Notes on the sheet:
  //   A
  //   B
  //   Inputs
  //   Output
  //   Ambos Positivos
  //   A negativo y B positivo
  //   A positivo y B negativo
  //   Ambos Negativos
endmodule

module Valor_Absoluto (
  input  [31:0] Input,
  output [31:0] Output
);

  wire [31:0] adder_1_out, not_1_out;

  assign not_1_out = ~Input;  // NOT_Gate not_1, 32 bits wide
  Adder #(.width(32)) adder_1 (.a(not_1_out), .b(32'h1), .out(adder_1_out));  // open: cin, cout
  Multiplexer #(.width(32)) multiplexer_1 (.in0(Input), .in1(adder_1_out), .out(Output), .sel(Input[31]));  // open: en
endmodule

module Register_File_MAIN (
  input  in_1,
  input  [4:0] in_2,
  input  [31:0] in_3,
  input  in_4,
  input  [4:0] in_5,
  input  in_6,
  input  [4:0] in_7,
  output [31:0] A,
  output [31:0] B,
  output [31:0] SP
);

  wire L0, L1, L2, L3, L4, L5, L6, L7, L8, L9, L10, L11, L12, L13, L14, L15, L16, L17, L18, L19, L20, L21,
       L22, L23, L24, L25, L26, L27, L28, L29, L30, L31;
  wire [31:0] Q0, Q1, Q2, Q3, Q4, Q5, Q6, Q7, Q8, Q9, Q10, Q11, Q12, Q13, Q14, Q15, Q16, Q17, Q18, Q19, Q20,
       Q21, Q22, Q23, Q24, Q25, Q26, Q27, Q28, Q29, Q30;

  Decoder #(.select(5), .disabled(0)) decoder_1 (
    .out0(L0), .out1(L1), .out2(L2), .out3(L3), .out4(L4), .out5(L5), .out6(L6), .out7(L7), .out8(L8),
    .out9(L9), .out10(L10), .out11(L11), .out12(L12), .out13(L13), .out14(L14), .out15(L15), .out16(L16),
    .out17(L17), .out18(L18), .out19(L19), .out20(L20), .out21(L21), .out22(L22), .out23(L23), .out24(L24),
    .out25(L25), .out26(L26), .out27(L27), .out28(L28), .out29(L29), .out30(L30), .out31(L31), .sel(in_2),
    .en(in_6));
  Multiplexer #(.select(5), .width(32), .enable("false")) multiplexer_1 (
    .in0(Q0), .in1(Q1), .in2(Q2), .in3(Q3), .in4(Q4), .in5(Q5), .in6(Q6), .in7(Q7), .in8(Q8), .in9(Q9),
    .in10(Q10), .in11(Q11), .in12(Q12), .in13(Q13), .in14(Q14), .in15(Q15), .in16(Q16), .in17(Q17),
    .in18(Q18), .in19(Q19), .in20(Q20), .in21(Q21), .in22(Q22), .in23(Q23), .in24(Q24), .in25(Q25),
    .in26(Q26), .in27(Q27), .in28(Q28), .in29(Q29), .in30(Q30), .in31(SP), .out(A), .sel(in_5));
  Multiplexer #(.select(5), .width(32), .enable("false")) multiplexer_2 (
    .in0(Q0), .in1(Q1), .in2(Q2), .in3(Q3), .in4(Q4), .in5(Q5), .in6(Q6), .in7(Q7), .in8(Q8), .in9(Q9),
    .in10(Q10), .in11(Q11), .in12(Q12), .in13(Q13), .in14(Q14), .in15(Q15), .in16(Q16), .in17(Q17),
    .in18(Q18), .in19(Q19), .in20(Q20), .in21(Q21), .in22(Q22), .in23(Q23), .in24(Q24), .in25(Q25),
    .in26(Q26), .in27(Q27), .in28(Q28), .in29(Q29), .in30(Q30), .in31(SP), .out(B), .sel(in_7));
  // Probe on in_5
  Register #(.width(32)) register_1 (.D({32{1'b0}}), .en(L0), .Q(Q0), .clk(in_1), .clr(in_4));
  Register #(.width(32)) register_2 (.D(in_3), .en(L3), .Q(Q3), .clk(in_1), .clr(in_4));
  Register #(.width(32)) register_3 (.D(in_3), .en(L6), .Q(Q6), .clk(in_1), .clr(in_4));
  Register #(.width(32)) register_4 (.D(in_3), .en(L9), .Q(Q9), .clk(in_1), .clr(in_4));
  Register #(.width(32)) register_5 (.D(in_3), .en(L12), .Q(Q12), .clk(in_1), .clr(in_4));
  Register #(.width(32)) register_6 (.D(in_3), .en(L15), .Q(Q15), .clk(in_1), .clr(in_4));
  Register #(.width(32)) register_7 (.D(in_3), .en(L18), .Q(Q18), .clk(in_1), .clr(in_4));
  Register #(.width(32)) register_8 (.D(in_3), .en(L21), .Q(Q21), .clk(in_1), .clr(in_4));
  Register #(.width(32)) register_9 (.D(in_3), .en(L24), .Q(Q24), .clk(in_1), .clr(in_4));
  Register #(.width(32)) register_10 (.D(in_3), .en(L27), .Q(Q27), .clk(in_1), .clr(in_4));
  Register #(.width(32)) register_11 (.D(in_3), .en(L30), .Q(Q30), .clk(in_1), .clr(in_4));
  Register #(.width(32)) register_12 (.D(in_3), .en(L1), .Q(Q1), .clk(in_1), .clr(in_4));
  Register #(.width(32)) register_13 (.D(in_3), .en(L4), .Q(Q4), .clk(in_1), .clr(in_4));
  Register #(.width(32)) register_14 (.D(in_3), .en(L7), .Q(Q7), .clk(in_1), .clr(in_4));
  Register #(.width(32)) register_15 (.D(in_3), .en(L10), .Q(Q10), .clk(in_1), .clr(in_4));
  Register #(.width(32)) register_16 (.D(in_3), .en(L13), .Q(Q13), .clk(in_1), .clr(in_4));
  Register #(.width(32)) register_17 (.D(in_3), .en(L16), .Q(Q16), .clk(in_1), .clr(in_4));
  Register #(.width(32)) register_18 (.D(in_3), .en(L19), .Q(Q19), .clk(in_1), .clr(in_4));
  Register #(.width(32)) register_19 (.D(in_3), .en(L22), .Q(Q22), .clk(in_1), .clr(in_4));
  Register #(.width(32)) register_20 (.D(in_3), .en(L25), .Q(Q25), .clk(in_1), .clr(in_4));
  Register #(.width(32)) register_21 (.D(in_3), .en(L28), .Q(Q28), .clk(in_1), .clr(in_4));
  Register #(.width(32)) register_22 (.D(in_3), .en(L2), .Q(Q2), .clk(in_1), .clr(in_4));
  Register #(.width(32)) register_23 (.D(in_3), .en(L5), .Q(Q5), .clk(in_1), .clr(in_4));
  Register #(.width(32)) register_24 (.D(in_3), .en(L8), .Q(Q8), .clk(in_1), .clr(in_4));
  Register #(.width(32)) register_25 (.D(in_3), .en(L11), .Q(Q11), .clk(in_1), .clr(in_4));
  Register #(.width(32)) register_26 (.D(in_3), .en(L4), .Q(Q14), .clk(in_1), .clr(in_4));
  Register #(.width(32)) register_27 (.D(in_3), .en(L17), .Q(Q17), .clk(in_1), .clr(in_4));
  Register #(.width(32)) register_28 (.D(in_3), .en(L20), .Q(Q20), .clk(in_1), .clr(in_4));
  Register #(.width(32)) register_29 (.D(in_3), .en(L23), .Q(Q23), .clk(in_1), .clr(in_4));
  Register #(.width(32)) register_30 (.D(in_3), .en(L26), .Q(Q26), .clk(in_1), .clr(in_4));
  Register #(.width(32)) register_31 (.D(in_3), .en(L29), .Q(Q29), .clk(in_1), .clr(in_4));
  Register #(.width(32)) register_32 (.D(in_3), .en(L31), .Q(SP), .clk(in_1), .clr(in_4));

  // Other names for the same wires on the sheet: CLK = in_1; DATA_INPUT[31:0] = in_3; DESTINATION_ADDRESS[4:0] = in_2;
  //   Q31[31:0] = SP; RST = in_4; RW = in_6; SA[4:0] = in_5; SB[4:0] = in_7

  // Notes on the sheet:
  //   REGISTER FILE
  //   REGISTERS
endmodule

module Hi_and_Low (
  input  in_1,
  input  in_2,
  input  in_3,
  input  [31:0] D_Low,
  input  [31:0] D_Hi,
  output [31:0] Low,
  output [31:0] Hi
);

  Register #(.width(32)) register_1 (.D(D_Low), .en(in_3), .Q(Low), .clk(in_1), .clr(in_2));
  Register #(.width(32)) register_2 (.D(D_Hi), .en(in_3), .Q(Hi), .clk(in_1), .clr(in_2));

  // Other names for the same wires on the sheet: clk = in_1; enable = in_3; rst = in_2

  // Notes on the sheet:
  //   Hi and Low Registers
endmodule

module Program_Counter_MAIN (
  input  [31:0] PC_prime,
  input  in_2,
  input  in_3,
  input  in_4,
  output [31:0] PC
);

  Register #(.width(32)) register_1 (.D(PC_prime), .en(in_2), .Q(PC), .clk(in_4), .clr(in_3));

  // Other names for the same wires on the sheet: clk = in_4; en = in_2; rst = in_3

  // Notes on the sheet:
  //   PROGRAM COUNTER
endmodule

module Branch_Control_MAIN (
  input  [31:0] PC,
  input  FC,
  input  jmp,
  input  [31:0] JZ,
  output [31:0] PC_prime
);

  wire [31:0] adder_1_out, adder_2_out, multiplexer_1_out;

  Adder #(.width(32)) adder_1 (.a(PC), .b(32'h4), .out(adder_1_out));  // open: cin, cout
  Multiplexer #(.width(32), .disabled(0), .enable("false")) multiplexer_1 (
    .in0({32{1'b0}}), .in1(JZ), .out(multiplexer_1_out), .sel(FC));
  Adder #(.width(32)) adder_2 (.a(adder_1_out), .b(multiplexer_1_out), .out(adder_2_out));  // open: cin, cout
  Multiplexer #(.width(32), .disabled(0), .enable("false")) multiplexer_2 (
    .in0(adder_2_out), .in1(JZ), .out(PC_prime), .sel(jmp));

  // Notes on the sheet:
  //   Branch Control
endmodule

module Instruction_Fetcher_MAIN (
  input  [31:0] in_1,
  input  [31:0] in_2,
  input  [31:0] in_3,
  input  [31:0] in_4,
  input  [31:0] in_5,
  output [15:0] RAM_Address,
  output [31:0] Instruction
);

  Multiplexer #(.select(2), .width(32), .enable("false")) multiplexer_1 (
    .in0(in_2), .in1(in_3), .in2(in_4), .in3(in_5),
    .out({Instruction[7:0], Instruction[15:8], Instruction[23:16], Instruction[31:24]}), .sel(in_1[3:2]));

  assign RAM_Address = in_1[19:4];

  // Other names for the same wires on the sheet: PC[31:0] = in_1; Instruction_Selector[1:0] = in_1[3:2];
  //   RAM_1[31:0] = in_2; RAM_2[31:0] = in_3; RAM_3[31:0] = in_4; RAM_4[31:0] = in_5

  // Notes on the sheet:
  //   Instruction Fetcher
endmodule

module Instruction_Decoder_MAIN (
  input  [31:0] Instruction,
  output R,
  output [5:0] Op_Code,
  output I,
  output [4:0] Rs,
  output J,
  output [4:0] Rt,
  output [4:0] Rd,
  output [15:0] Const,
  output [25:0] Dest_salto,
  output [5:0] Func_Code,
  output halt,
  output push,
  output tty,
  output pop,
  output rdm,
  output kbd_en,
  output jr,
  output lw,
  output sw,
  output HiLo_Sel,
  output RF_W,
  output Load_HiLo
);

  wire and_1_out, and_2_out, and_7_out, comparator_1_eq, comparator_2_eq, comparator_3_eq, comparator_5_eq,
       comparator_6_eq, comparator_7_eq, comparator_8_eq, comparator_9_eq, comparator_11_eq,
       comparator_12_eq, comparator_13_eq, comparator_14_eq, comparator_15_eq, comparator_16_gt,
       comparator_17_lt, nor_1_out, or_1_out;

  Comparator #(.width(6)) comparator_1 (.a(Instruction[31:26]), .b({6{1'b1}}), .eq(comparator_1_eq));  // open: gt, lt
  Comparator #(.width(6)) comparator_2 (.a(Instruction[31:26]), .b({6{1'b0}}), .eq(comparator_2_eq));  // open: gt, lt
  Comparator #(.width(6)) comparator_3 (.a(Instruction[5:0]), .b({6{1'b0}}), .eq(comparator_3_eq));  // open: gt, lt
  Comparator #(.width(6)) comparator_4 (.a(Instruction[31:26]), .b(6'b101011), .eq(sw));  // open: gt, lt
  Comparator #(.width(3), .mode("unsigned")) comparator_5 (
    .a(Instruction[31:29]), .b(3'b001), .eq(comparator_5_eq));  // open: gt, lt
  and and_1 (and_1_out, comparator_2_eq, comparator_3_eq);
  Comparator #(.width(6)) comparator_6 (.a(Instruction[5:0]), .b({6{1'b1}}), .eq(comparator_6_eq));  // open: gt, lt
  Comparator #(.width(6)) comparator_7 (.a(Instruction[5:0]), .b(6'b000001), .eq(comparator_7_eq));  // open: gt, lt
  Comparator #(.width(6)) comparator_8 (.a(Instruction[5:0]), .b(6'b000010), .eq(comparator_8_eq));  // open: gt, lt
  Comparator #(.width(6)) comparator_9 (.a(Instruction[5:0]), .b(6'b000100), .eq(comparator_9_eq));  // open: gt, lt
  and and_2 (and_2_out, I, comparator_5_eq);
  nor nor_1 (nor_1_out, halt, tty, jr, Load_HiLo, and_1_out);
  and and_3 (halt, comparator_6_eq, comparator_1_eq);
  and and_4 (tty, comparator_7_eq, comparator_1_eq);
  and and_5 (rdm, comparator_8_eq, comparator_1_eq);
  and and_6 (kbd_en, comparator_1_eq, comparator_9_eq);
  Comparator #(.width(6)) comparator_10 (.a(Instruction[31:26]), .b(6'b100011), .eq(lw));  // open: gt, lt
  or or_1 (or_1_out, lw, and_2_out);
  and and_7 (and_7_out, R, nor_1_out);
  Type_Decoder type_decoder_1 (.Op_Code(Instruction[31:26]), .R(R), .I(I), .J(J));
  or or_2 (RF_W, or_1_out, and_7_out);
  Comparator #(.width(6)) comparator_11 (.a(Instruction[31:26]), .b(6'b111000), .eq(comparator_11_eq));  // open: gt, lt
  // Probe on 6'b010111
  Comparator #(.width(6)) comparator_12 (.a(Instruction[5:0]), .b(6'b000001), .eq(comparator_12_eq));  // open: gt, lt
  Comparator #(.width(6)) comparator_13 (.a(Instruction[5:0]), .b({6{1'b0}}), .eq(comparator_13_eq));  // open: gt, lt
  Comparator #(.width(6)) comparator_14 (.a(Instruction[5:0]), .b(6'b001000), .eq(comparator_14_eq));  // open: gt, lt
  Comparator #(.width(6)) comparator_15 (.a(Instruction[5:0]), .b(6'b010000), .eq(comparator_15_eq));  // open: gt, lt
  // Probe on 6'b011100
  and and_8 (push, comparator_12_eq, comparator_11_eq);
  and and_9 (pop, comparator_11_eq, comparator_13_eq);
  and and_10 (jr, comparator_14_eq, R);
  and and_11 (HiLo_Sel, comparator_15_eq, R);
  Comparator #(.width(6), .mode("unsigned")) comparator_16 (
    .a(Instruction[5:0]), .b(6'b010111), .gt(comparator_16_gt));  // open: eq, lt
  Comparator #(.width(6), .mode("unsigned")) comparator_17 (
    .a(Instruction[5:0]), .b(6'b011100), .lt(comparator_17_lt));  // open: gt, eq
  and and_12 (Load_HiLo, R, comparator_16_gt, comparator_17_lt);

  assign Const = Instruction[15:0];
  assign Dest_salto = Instruction[25:0];
  assign Func_Code = Instruction[5:0];
  assign Op_Code = Instruction[31:26];
  assign Rd = Instruction[15:11];
  assign Rs = Instruction[25:21];
  assign Rt = Instruction[20:16];

  // Other names for the same wires on the sheet: Hilo_L = Load_HiLo

  // Notes on the sheet:
  //   not operation
  //   Instruction Decoder
endmodule

module Type_Decoder (
  input  [5:0] Op_Code,
  output R,
  output I,
  output J
);

  wire and_2_out, and_3_out, and_4_out, or_2_out, or_3_out, or_4_out, or_5_out;

  and and_1 (J, ~Op_Code[0], Op_Code[1], ~Op_Code[2], ~Op_Code[4], ~Op_Code[5], ~Op_Code[3]);  // AND_Gate
  and and_2 (and_2_out, ~Op_Code[0], ~Op_Code[1], ~Op_Code[2], Op_Code[4], Op_Code[5], Op_Code[3]);  // AND_Gate
  and and_3 (and_3_out, ~Op_Code[0], ~Op_Code[1], ~Op_Code[2], ~Op_Code[4], ~Op_Code[5], ~Op_Code[3]);  // AND_Gate
  and and_4 (and_4_out, Op_Code[0], Op_Code[1], Op_Code[2], Op_Code[4], Op_Code[5], Op_Code[3]);
  or or_1 (R, and_2_out, and_3_out, and_4_out);
  or or_2 (or_2_out, Op_Code[0], Op_Code[1], Op_Code[2], Op_Code[4], Op_Code[5], Op_Code[3]);
  or or_3 (or_3_out, ~Op_Code[0], ~Op_Code[1], ~Op_Code[2], ~Op_Code[4], ~Op_Code[5], ~Op_Code[3]);  // OR_Gate
  or or_4 (or_4_out, Op_Code[0], Op_Code[1], Op_Code[2], ~Op_Code[4], ~Op_Code[5], ~Op_Code[3]);  // OR_Gate
  or or_5 (or_5_out, Op_Code[0], ~Op_Code[1], Op_Code[2], Op_Code[4], Op_Code[5], Op_Code[3]);  // OR_Gate
  and and_5 (I, or_2_out, or_3_out, or_4_out, or_5_out);

  // Notes on the sheet:
  //   Op Code
  //   00 0000
  //   11 1000
  //   11 1111
  //   00 1000
  //   00 1100
  //   00 1010
  //   00 0100
  //   00 0101
  //   00 0110
  //   00 0111
  //   00 0001
  //   10 0011
  //   10 1011
  //   00 0010
  //   R
  //   I
  //   0
  //   1
  //   0
  //   1
  //   0
  //   1
  //   0
  //   1
  //   0
  //   1
  //   0
  //   1
  //   1
  //   0
  //   1
  //   0
  //   1
  //   0
  //   0
  //   1
  //   1
  //   0
  //   1
  //   0
  //   0
  //   1
  //   0
  //   0
  //   J
  //   0
  //   0
  //   0
  //   0
  //   0
  //   0
  //   0
  //   0
  //   0
  //   0
  //   0
  //   0
  //   0
  //   1
  //   Entrada
  //   Salidas
endmodule

module Constant_Completer_MAIN (
  input  [5:0] in_1,
  input  [15:0] in_2,
  output [31:0] k
);

  wire comparator_1_eq, comparator_2_eq, comparator_3_eq, or_1_out;
  wire [1:0] priority_encoder_1_out;
  wire [31:0] sign_k, zero_k;
  wire [31:18] branch_k;

  assign branch_k = {{13{in_2[15]}}, in_2[15]};  // Bit_Extender bit_extender_1
  Comparator #(.width(6), .mode("unsigned")) comparator_1 (
    .a(in_1), .b(6'b000001), .eq(comparator_1_eq));  // open: gt, lt
  or or_1 (or_1_out, comparator_1_eq, comparator_2_eq);
  Comparator #(.width(2), .mode("unsigned")) comparator_2 (
    .a(in_1[3:2]), .b(2'b01), .eq(comparator_2_eq));  // open: gt, lt
  Comparator #(.width(2), .mode("unsigned")) comparator_3 (
    .a(in_1[3:2]), .b(2'b11), .eq(comparator_3_eq));  // open: gt, lt
  assign zero_k = {{16{1'b0}}, in_2};  // Bit_Extender bit_extender_2
  assign sign_k = {{16{in_2[15]}}, in_2};  // Bit_Extender bit_extender_3
  Priority_Encoder #(.select(2)) priority_encoder_1 (
    .in0(1'b1), .in1(or_1_out), .in2(comparator_3_eq), .out(priority_encoder_1_out));  // open: in3, gs, en_out, en_in
  // Probe on priority_encoder_1_out
  Multiplexer #(.select(2), .width(32), .enable("false")) multiplexer_1 (
    .in0(sign_k), .in1({branch_k, in_2, 2'b00}), .in2(zero_k), .out(k), .sel(priority_encoder_1_out));  // open: in3

  // Other names for the same wires on the sheet: branch_k[17:2] = in_2; const[15:0] = in_2; bit_15 = in_2[15];
  //   op_code[5:0] = in_1

  // Notes on the sheet:
  //   bit 2 y3
  //   Constant Completer
  //   sign k
  //   100011
  //   101011
  //   001010
  //   001011
  //   001000
  //   zero k
  //   001100
  //   001101
  //   001110
  //   branch k
  //   000100
  //   000101
  //   000110
  //   000111
  //   000001
endmodule

module Jumper_MAIN (
  input  [31:0] k,
  input  [31:0] Rs,
  input  [31:0] PC,
  input  [25:0] dest,
  input  jr,
  input  J,
  output out_7,
  output [31:0] jmp_size
);

  wire undriven;
  wire [1:0] priority_encoder_1_out;

  or or_1 (out_7, jr, J);
  // Probe on undriven
  Priority_Encoder #(.select(2)) priority_encoder_1 (
    .in0(1'b1), .in1(jr), .in2(J), .out(priority_encoder_1_out));  // open: in3, gs, en_out, en_in
  Multiplexer #(.select(2), .width(32), .enable("false")) multiplexer_1 (
    .in0(k), .in1(Rs), .in2({PC[31:28], dest, 2'b00}), .out(jmp_size), .sel(priority_encoder_1_out));  // open: in3
  // Probe on priority_encoder_1_out

  // Other names for the same wires on the sheet: jmp_dir = out_7

  // Notes on the sheet:
  //   Jumper
endmodule

module Control_Unit_MAIN (
  input  in_1,
  input  in_2,
  input  in_3,
  input  [3:0] in_4,
  input  in_5,
  input  in_6,
  input  [3:0] in_7,
  input  in_8,
  input  in_9,
  input  in_10,
  output Ch_SP,
  output load_ALU,
  output CS,
  output out_14,
  output W_RF,
  output PC_Load,
  output END,
  output IR_Load,
  output clr_instr,
  output DATA_Load,
  output I_O_D
);

  wire Ch_SP_1, Ch_SP_2, CS_1, CS_2, d_ff_1_q, d_ff_3_q, demultiplexer_1_out0, demultiplexer_1_out1,
       demultiplexer_2_out0, demultiplexer_3_out0, demultiplexer_3_out1, demultiplexer_4_out0,
       demultiplexer_4_out1, demultiplexer_5_out0, demultiplexer_5_out1, demultiplexer_6_out0,
       demultiplexer_7_out0, demultiplexer_8_out1, demultiplexer_9_out0, end_R0, end_R1, end_W, EXECUTE_q,
       load_ALU_1, load_ALU_2, or_1_out, or_2_out, or_5_out, or_8_out, or_9_out, or_10_out, or_11_out,
       or_12_out, W_RF_1, W_RF_3, WAIT_3_q;

  Demultiplexer #(.disabled(0), .enable("false")) demultiplexer_1 (
    .out0(demultiplexer_1_out0), .out1(demultiplexer_1_out1), .in(d_ff_1_q), .sel(in_10));
  D_Flip_Flop d_ff_1 (.clk(in_1), .D(demultiplexer_1_out0), .Q(d_ff_1_q), .preset(in_8));  // open: Qn, en, reset
  or or_1 (or_1_out, PC_Load, demultiplexer_1_out1);
  D_Flip_Flop FETCH (.clk(in_1), .D(or_1_out), .Q(clr_instr), .reset(in_8));  // open: Qn, preset, en
  or or_2 (or_2_out, demultiplexer_2_out0, clr_instr);
  D_Flip_Flop \wait  (.clk(in_1), .D(or_2_out), .Q(CS_1), .reset(in_8));  // open: Qn, preset, en
  Demultiplexer #(.disabled(0), .enable("false")) demultiplexer_2 (
    .out0(demultiplexer_2_out0), .out1(IR_Load), .in(CS_1), .sel(end_R0));
  Timer timer_1 (.in_1(in_7), .in_2(in_1), .in_3(PC_Load), .in_4(clr_instr), .\end (end_R0));
  Demultiplexer #(.enable("false")) demultiplexer_3 (
    .out0(demultiplexer_3_out0), .out1(demultiplexer_3_out1), .in(IR_Load), .sel(in_9));
  or or_3 (Ch_SP, Ch_SP_1, Ch_SP_2);
  or or_4 (CS, CS_1, CS_2, out_14);
  or or_5 (or_5_out, demultiplexer_3_out0, demultiplexer_3_out1);
  D_Flip_Flop d_ff_2 (.clk(in_1), .Q(Ch_SP_1), .preset(demultiplexer_3_out1), .reset(PC_Load));  // open: D, Qn, en
  D_Flip_Flop EXECUTE (.clk(in_1), .D(or_5_out), .Q(EXECUTE_q), .reset(in_8));  // open: Qn, preset, en
  Demultiplexer #(.disabled(0), .enable("false")) demultiplexer_4 (
    .out0(demultiplexer_4_out0), .out1(demultiplexer_4_out1), .in(EXECUTE_q), .sel(in_3));
  or or_6 (load_ALU, load_ALU_2, load_ALU_1);
  or or_7 (W_RF, W_RF_1, W_RF_3, load_ALU_2);
  or or_8 (or_8_out, END, demultiplexer_4_out1);
  Demultiplexer #(.disabled(0), .enable("false")) demultiplexer_5 (
    .out0(demultiplexer_5_out0), .out1(demultiplexer_5_out1), .in(demultiplexer_4_out0), .sel(in_2));
  D_Flip_Flop u_END (.clk(in_1), .D(or_8_out), .Q(END), .reset(in_8));  // open: Qn, preset, en
  or or_9 (or_9_out, demultiplexer_6_out0, demultiplexer_5_out1);
  D_Flip_Flop WAIT_2 (.clk(in_1), .D(or_9_out), .Q(CS_2), .reset(in_8));  // open: Qn, preset, en
  Timer timer_2 (.in_1(in_7), .in_2(in_1), .in_3(PC_Load), .in_4(demultiplexer_5_out1), .\end (end_R1));
  Demultiplexer #(.disabled(0), .enable("false")) demultiplexer_6 (
    .out0(demultiplexer_6_out0), .out1(DATA_Load), .in(CS_2), .sel(end_R1));
  D_Flip_Flop WAIT_3 (.clk(in_1), .D(DATA_Load), .Q(WAIT_3_q), .reset(in_8));  // open: Qn, preset, en
  Demultiplexer #(.disabled(0), .enable("false")) demultiplexer_7 (
    .out0(demultiplexer_7_out0), .out1(W_RF_3), .in(WAIT_3_q), .sel(in_6));
  D_Flip_Flop d_ff_3 (.clk(in_1), .D(W_RF_3), .Q(d_ff_3_q), .reset(PC_Load));  // open: Qn, preset, en
  D_Flip_Flop WAIT_4 (.clk(in_1), .D(d_ff_3_q), .Q(Ch_SP_2), .reset(in_8));  // open: Qn, preset, en
  or or_10 (or_10_out, demultiplexer_5_out0, demultiplexer_7_out0, Ch_SP_2);
  Demultiplexer #(.disabled(0), .enable("false")) demultiplexer_8 (
    .out0(load_ALU_2), .out1(demultiplexer_8_out1), .in(or_10_out), .sel(in_5));
  or or_11 (or_11_out, demultiplexer_9_out0, demultiplexer_8_out1);
  Timer timer_3 (.in_1(in_7), .in_2(in_1), .in_3(PC_Load), .in_4(demultiplexer_8_out1), .\end (end_W));
  D_Flip_Flop WAIT_5 (.clk(in_1), .D(or_11_out), .Q(out_14), .reset(in_8));  // open: Qn, preset, en
  Demultiplexer #(.disabled(0), .enable("false")) demultiplexer_9 (
    .out0(demultiplexer_9_out0), .out1(load_ALU_1), .in(out_14), .sel(end_W));
  D_Flip_Flop d_ff_4 (.clk(in_1), .D(load_ALU_1), .Q(W_RF_1));  // open: Qn, preset, en, reset
  or or_12 (or_12_out, load_ALU_2, W_RF_1);
  D_Flip_Flop NEXT (.clk(in_1), .D(or_12_out), .Q(PC_Load), .reset(in_8));  // open: Qn, preset, en

  assign I_O_D = in_2;

  // Other names for the same wires on the sheet: clk = in_1; halt = in_3; W_RF_2 = load_ALU_2; pop = in_6;
  //   push = in_9; R_RAM = in_2; CS_3 = out_14; RAM_R_W = out_14; rst = in_8; rst_waiter = PC_Load; RT[3:0] = in_7;
  //   start = in_10; W_RAM = in_5; WT[3:0] = in_4

  // Notes on the sheet:
  //   Control Unit
endmodule

module Timer (
  input  [3:0] in_1,
  input  in_2,
  input  in_3,
  input  in_4,
  output \end 
);

  wire and_1_out, d_ff_1_q, not_1_out;
  wire [3:0] i;

  D_Flip_Flop #(.trigger("falling")) d_ff_1 (.clk(in_2), .Q(d_ff_1_q), .preset(in_4), .reset(in_3));  // open: D, Qn, en
  not not_1 (not_1_out, \end );
  Counter #(.width(4), .max('hf), .ongoal("stay")) counter (
    .count(and_1_out), .Q(i), .clk(in_2), .clr(in_3));  // open: load, D, carry
  and and_1 (and_1_out, d_ff_1_q, not_1_out);
  Comparator #(.width(4), .mode("unsigned")) comparator_1 (.a(i), .b(in_1), .gt(\end ));  // open: eq, lt

  // Other names for the same wires on the sheet: clk = in_2; rst = in_3; start = in_4; t[3:0] = in_1

  // Notes on the sheet:
  //   TIMER
endmodule

module RAM_Writer_MAIN (
  input  [31:0] in_1,
  output [3:0] mask,
  output [15:0] adr
);

  Multiplexer #(.select(2), .width(4), .disabled(0), .enable("false")) multiplexer_1 (
    .in0(4'b0001), .in1(4'b0010), .in2(4'b0100), .in3(4'b1000), .out(mask), .sel(in_1[3:2]));

  assign adr = in_1[19:4];

  // Notes on the sheet:
  //   RAM WRITER
endmodule

module Flag_Condition_2 (
  input  [5:0] OP_Code,
  input  Equal_Flag,
  input  Less_than_0,
  output Flag_Condition
);

  wire and_1_out, and_2_out, and_3_out, and_4_out, and_5_out, or_1_out;

  or or_1 (or_1_out, Less_than_0, Equal_Flag);
  and and_1 (and_1_out, ~OP_Code[0], ~OP_Code[1], OP_Code[2], ~OP_Code[3], ~OP_Code[4], ~OP_Code[5], Equal_Flag);  // AND_Gate
  and and_2 (and_2_out, OP_Code[0], ~OP_Code[1], OP_Code[2], ~OP_Code[3], ~OP_Code[4], ~OP_Code[5], ~Equal_Flag);  // AND_Gate
  and and_3 (and_3_out, ~OP_Code[0], OP_Code[1], OP_Code[2], ~OP_Code[3], ~OP_Code[4], ~OP_Code[5], or_1_out);  // AND_Gate
  and and_4 (and_4_out, OP_Code[0], OP_Code[1], OP_Code[2], ~OP_Code[3], ~OP_Code[4], ~OP_Code[5], ~Equal_Flag, ~Less_than_0);  // AND_Gate
  and and_5 (and_5_out, OP_Code[0], ~OP_Code[1], ~OP_Code[2], ~OP_Code[3], ~OP_Code[4], ~OP_Code[5], ~Equal_Flag, Less_than_0);  // AND_Gate
  or or_2 (Flag_Condition, and_1_out, and_2_out, and_3_out, and_4_out, and_5_out);

  // Other names for the same wires on the sheet: EQ = Equal_Flag; FC = Flag_Condition; OP[5:0] = OP_Code;
  //   ST_0 = Less_than_0
endmodule
